# Fritzing sketch Sketch (saved by Fritzing 0.9.2b)
circuit board: 8.46667cm x 5.64444cm
breadboards: 1

parts:
  Arduino = Arduino Uno (Rev3)
  LED = LED - 5mm [color="Red (633nm)" package="5 mm [THT]"]
  Resistor = Resistor [tolerance=±5% resistance=22 package=THT]

nets:
  N1: Arduino.GND, LED.cathode
  N2: Arduino.5V, Resistor.Pin_0
  N3: LED.anode, Resistor.Pin_1
