# Fritzing sketch Sketch (saved by Fritzing 0.9.3b)
circuit board: 8.46667cm x 5.64444cm
breadboards: 1

parts:
  Part1 = Arduino Uno (Rev3)
  LED1 = LED - 5mm [color="Red (633nm)" package="5 mm [THT]"]
  Resistor1 = Resistor [tolerance=±5% resistance=22 package=THT]
  LED2 = LED - 5mm [color="Red (633nm)" package="5 mm [THT]"]
  Resistor2 = Resistor [tolerance=±5% resistance=22 package=THT]
  LED3 = LED - 5mm [color="Red (633nm)" package="5 mm [THT]"]
  Resistor3 = Resistor [tolerance=±5% resistance=22 package=THT]
  LED4 = LED - 5mm [color="Red (633nm)" package="5 mm [THT]"]
  Resistor4 = Resistor [tolerance=±5% resistance=22 package=THT]
  LED5 = LED - 5mm [color="Red (633nm)" package="5 mm [THT]"]
  Resistor5 = Resistor [tolerance=±5% resistance=22 package=THT]
  T1 = TMP36 Temperature Sensor [package="TO92 [THT]"]

nets:
  N1: Part1.A0, T1.Vout
  GND: Part1.GND, Resistor1.Pin_0, Resistor2.Pin_0, Resistor3.Pin_0, Resistor4.Pin_0, Resistor5.Pin_0, T1.GND
  N2: Part1.D2, LED1.anode
  N3: Part1.D3_PWM, LED2.anode
  N4: Part1.D4, LED3.anode
  N5: Part1.D5_PWM, LED4.anode
  N6: Part1.D6_PWM, LED5.anode
  N7: Part1.5V, T1.+Vs
  N8: LED1.cathode, Resistor1.Pin_1
  N9: LED2.cathode, Resistor2.Pin_1
  N10: LED3.cathode, Resistor3.Pin_1
  N11: LED4.cathode, Resistor4.Pin_1
  N12: LED5.cathode, Resistor5.Pin_1
