# Fritzing sketch Sketch (saved by Fritzing 0.9.3b)
breadboards: 1

parts:
  Part2 = Arduino Uno (Rev3)
  LED6 = LED - 5mm [color="Red (633nm)" package="5 mm [THT]"]
  Resistor6 = Resistor [tolerance=±5% resistance=22 package=THT]
  S1 = Pushbutton [package="[THT]"]
  R2 = Resistor [tolerance=±5% resistance=10k package=THT]
  R5 = Photocell (LDR) [package=THT]
  R6 = Photocell (LDR) [package=THT]
  R7 = Photocell (LDR) [package=THT]
  R8 = Resistor [tolerance=±5% resistance=10k package=THT]
  R9 = Resistor [tolerance=±5% resistance=10k package=THT]
  R10 = Resistor [tolerance=±5% resistance=220 package=THT]
  R11 = Resistor [tolerance=±5% resistance=220 package=THT]
  R12 = Resistor [tolerance=±5% resistance=220 package=THT]
  LED7 = RGB LED (com. cathode, rgb) [package="5 mm [THT]"]
  R1 = Resistor [tolerance=±5% resistance=10k package=THT]

nets (from the schematic view):
  N1: Part2.A0, R7.pin_1, R9.Pin_0
  N2: Part2.A1, R2.Pin_0, R5.pin_1
  N3: Part2.A2, R6.pin_0, R8.Pin_1
  N4: Part2.D9_PWM, R10.Pin_0
  N5: Part2.D10_PWM/SS, R11.Pin_0
  N6: Part2.D11_PWM/MOSI, R12.Pin_0
  N7: Part2.D12/MISO, Resistor6.Pin_1, S1.Pin_1, S1.Pin_2, R1.Pin_1
  N8: Part2.GND, LED6.cathode, R2.Pin_1, R8.Pin_0, R9.Pin_1, LED7.common_cathode, R1.Pin_0
  N9: Part2.5V, S1.Pin_3, S1.Pin_4, R5.pin_0, R6.pin_1, R7.pin_0
  N10: LED6.anode, Resistor6.Pin_0
  N11: R10.Pin_1, LED7.blue_anode
  N12: R11.Pin_1, LED7.green_anode
  N13: R12.Pin_1, LED7.red_anode
