# Fritzing sketch Sketch (saved by Fritzing 0.9.3b)
breadboards: 1

parts:
  Part3 = Arduino Uno (Rev3)
  LED7 = LED - 5mm [color="Green (555nm)" package="5 mm [THT]"]
  LED8 = LED - 5mm [color="Yellow (585nm)" package="5 mm [THT]"]
  LED9 = LED - 5mm [color="Red (633nm)" package="5 mm [THT]"]
  Resistor7 = Resistor [tolerance=±5% resistance=22 package=THT]
  Resistor8 = Resistor [tolerance=±5% resistance=22 package=THT]
  Resistor9 = Resistor [tolerance=±5% resistance=22 package=THT]
  C1 = Capacitor Polarized [package=cpol-radial-100uf-25v]
  C2 = Capacitor Polarized [package=cpol-radial-100uf-25v]
  J1 = Basic Servo
  R1 = Rotary Potentiometer (Small) [maximum_resistance=100kΩ package=THT]

nets:
  N1: Part3.A0, R1.wiper
  N2: Part3.D9_PWM, J1.pulse
  N3: Part3.D2, LED9.anode
  N4: Part3.D3_PWM, LED8.anode
  N5: Part3.D4, LED7.anode
  5V: Part3.5V, C1.+, C2.+, J1.vcc, R1.leg1
  GND: Part3.GND, Resistor7.Pin_0, Resistor8.Pin_0, Resistor9.Pin_0, C1.-, C2.-, J1.gnd, R1.leg2
  N6: LED7.cathode, Resistor8.Pin_1
  N7: LED8.cathode, Resistor9.Pin_1
  N8: LED9.cathode, Resistor7.Pin_1
